# Fritzing sketch CeilingFan (saved by Fritzing 0.9.9b)
circuit board: 15.8891cm x 8.04337cm
breadboards: 1

parts:
  PCA9685 = PCA9685 16x12-bit PWM Breakout
  Relay_module = Module 4 Relais 5V [package="Module 4 Relais 5V"]
  J1 = female pin header, 15 pins [form="♀ (female)"]
  J2 = female pin header, 15 pins [form="♀ (female)"]
  Mod1 = Amica NodeMCU DEVKIT 1.0

nets:
  N1: PCA9685.no_name_yet#501, Relay_module.GND, J1.pin14, J2.pin10, J2.pin14, Mod1.pin2, Mod1.pin_9, Mod1.pin_25, Mod1.pin_29
  N2: PCA9685.no_name_yet#503, Mod1.pin_14
  N3: PCA9685.no_name_yet#504, Mod1.pin_13
  N4: PCA9685.no_name_yet#505, Mod1.pin1, Mod1.pin_10, Mod1.pin_26
  N5: Relay_module.VCC, Mod1.pin_30
  N6: Relay_module.IN1, Mod1.pin7
  N7: Relay_module.IN2, Mod1.pin6
  N8: Relay_module.IN3, Mod1.pin8
  N9: Relay_module.IN4, Mod1.pin5

custom parts:
  Module 4 Relais 5V: Module 4 Relais 5V 4x SPD-06VDC-SD-C
  Amica NodeMCU DEVKIT 1.0: Amica NodeMCU DEVKIT 1.0 Development Kit based on ESP8266 ESP-12E, integating GPIO, PWM, IIC, 1-Wire and ADC all in one board. Links: NodeMCU information page Github
